# Fritzing sketch 2map 2019 october (saved by Fritzing 0.9.3b)
circuit board: 4.38629cm x 2.35657cm
breadboards: 1

parts:
  ZIF_SOCKET1 = Aries 28-6574-10 28W ZIF Socket [part_number=28-6574-10]
  ZIF_SOCKET2 = Aries 28-6574-10 28W ZIF Socket [part_number=28-6574-10]
  R1 = Resistor [tolerance=±5% resistance=220 package=THT]
  J1 = female pin header, 2 pins [form="♀ (female)"]

nets:
  N1: ZIF_SOCKET1.Pin_1, R1.Pin_0, J1.pin2
  N2: ZIF_SOCKET1.Pin_2, ZIF_SOCKET2.Pin_2
  N3: ZIF_SOCKET1.Pin_3, ZIF_SOCKET2.Pin_3
  N4: ZIF_SOCKET1.Pin_4, ZIF_SOCKET2.Pin_4
  N5: ZIF_SOCKET1.Pin_5, ZIF_SOCKET2.Pin_5
  N6: ZIF_SOCKET1.Pin_6, ZIF_SOCKET2.Pin_6
  N7: ZIF_SOCKET1.Pin_7, ZIF_SOCKET2.Pin_7
  N8: ZIF_SOCKET1.Pin_8, ZIF_SOCKET2.Pin_8
  N9: ZIF_SOCKET1.Pin_9, ZIF_SOCKET2.Pin_9
  N10: ZIF_SOCKET1.Pin_10, ZIF_SOCKET2.Pin_10
  N11: ZIF_SOCKET1.Pin_11, ZIF_SOCKET2.Pin_11
  N12: ZIF_SOCKET1.Pin_12, ZIF_SOCKET2.Pin_12
  N13: ZIF_SOCKET1.Pin_13, ZIF_SOCKET2.Pin_13
  N14: ZIF_SOCKET1.Pin_14, ZIF_SOCKET2.Pin_14, J1.pin1
  N15: ZIF_SOCKET1.Pin_15, ZIF_SOCKET2.Pin_15
  N16: ZIF_SOCKET1.Pin_16, ZIF_SOCKET2.Pin_16
  N17: ZIF_SOCKET1.Pin_17, ZIF_SOCKET2.Pin_17
  N18: ZIF_SOCKET1.Pin_18, ZIF_SOCKET2.Pin_18
  N19: ZIF_SOCKET1.Pin_19, ZIF_SOCKET2.Pin_19
  N20: ZIF_SOCKET1.Pin_20, ZIF_SOCKET2.Pin_20
  N21: ZIF_SOCKET1.Pin_21, ZIF_SOCKET2.Pin_21
  N22: ZIF_SOCKET1.Pin_22, ZIF_SOCKET2.Pin_22
  N23: ZIF_SOCKET1.Pin_23, ZIF_SOCKET2.Pin_23
  N24: ZIF_SOCKET1.Pin_24, ZIF_SOCKET2.Pin_24
  N25: ZIF_SOCKET1.Pin_25, ZIF_SOCKET2.Pin_25
  N26: ZIF_SOCKET1.Pin_26, ZIF_SOCKET2.Pin_26
  N27: ZIF_SOCKET1.Pin_27, ZIF_SOCKET2.Pin_27
  N28: ZIF_SOCKET1.Pin_28, ZIF_SOCKET2.Pin_28
  N29: ZIF_SOCKET2.Pin_1, R1.Pin_1
