# Fritzing sketch plcc32t-dip28 V3 (saved by Fritzing 0.9.3b)
circuit board: 1.91712cm x 3.54991cm
breadboards: 1

parts:
  J9 = female pin header, 3 pins [form="♀ (female)"]
  J5 = female pin header, 6 pins [form="♀ (female)"]
  J6 = female pin header, 6 pins [form="♀ (female)"]
  J10 = female pin header, 3 pins [form="♀ (female)"]
  J7 = female pin header, 2 pins [form="♀ (female)"]
  J4 = female pin header, 7 pins [form="♀ (female)"]
  J3 = female pin header, 7 pins [form="♀ (female)"]
  J8 = female pin header, 2 pins [form="♀ (female)"]
  J2 = female pin header, 14 pins [form="♀ (female)"]
  J1 = female pin header, 14 pins [form="♀ (female)"]

nets:
  N1: J9.pin1, J2.pin6
  N2: J9.pin2, J2.pin8
  N3: J9.pin3, J2.pin10
  N4: J5.pin1, J1.pin4
  N5: J5.pin4, J2.pin2
  N6: J5.pin6, J2.pin4
  N7: J6.pin1, J1.pin11
  N8: J6.pin3, J1.pin13
  N9: J6.pin6, J2.pin11
  N10: J10.pin1, J1.pin6
  N11: J10.pin2, J1.pin7
  N12: J10.pin3, J1.pin9
  N13: J7.pin1, J1.pin1
  N14: J7.pin2, J2.pin1
  N15: J4.pin1, J2.pin3
  N16: J4.pin2, J2.pin5
  N17: J4.pin3, J2.pin7
  N18: J4.pin4, J2.pin9
  N19: J4.pin6, J2.pin13
  N20: J4.pin7, J2.pin12
  N21: J3.pin1, J1.pin3
  N22: J3.pin2, J1.pin2
  N23: J3.pin3, J1.pin5
  N24: J3.pin5, J1.pin8
  N25: J3.pin6, J1.pin10
  N26: J3.pin7, J1.pin12
  N27: J8.pin1, J1.pin14
  N28: J8.pin2, J2.pin14

notes:
  Plcc to Dip28
